# Fritzing sketch Bioe3090_Incubator_Schematic (saved by Fritzing 0.9.2b)
breadboards: 1

parts:
  Part1 = Arduino Uno (Rev3)
  Syringe_Heater = Peltier Element
  Q3 = MOSFET-NCHANNEL [package=to220v]  # not connected
  DS1 = DS18B20 1-Wire Temperature Sensor [part_number=DS18B20]
  Pullup = Resistor [tolerance=±5% resistance=4.7k package="1206 [SMD]"]
  J1 = Power Jack [package=power_jack_combo]
  Pulldown = Resistor [tolerance=±5% resistance=10k package=THT]
  DS2 = DS18B20 1-Wire Temperature Sensor [part_number=DS18B20]  # not connected

nets:
  GND: Part1.GND, DS1.GND, J1.GND, Pulldown.Pin_0
  N1: Part1.D6_PWM, Pulldown.Pin_1
  N2: Part1.D7, DS1.DQ, Pullup.Pin_1
  5V: Part1.5V, DS1.VDD, Pullup.Pin_0
  N3: Syringe_Heater.pin2, J1.GNDBREAK

notes:
  5V Power from Wall-Wart
